// Logisim project ExemploPortaAnd.circ as structural Verilog: 1 circuit, main circuit main
module main (
  input  A,
  input  B,
  input  C,
  output out_4,
  output out_5,
  output out_6,
  output out_7
);

  and A_B (out_6, A, B);
  and A_B_2 (out_4, A, B);
  and A_B_C (out_5, A, B, C);
  and A_B__C (out_7, out_6, C);
endmodule
